// Logisim project Processador_Arquitetura.circ as structural Verilog: 25 circuits, main circuit main
module main (
  input  R,
  output [31:0] out_2,
  output [31:0] out_3,
  output [31:0] out_4,
  output [1:0] out_5,
  output [4:0] out_6,
  output [1:0] out_7,
  output [31:0] out_8,
  output [1:0] out_9,
  output [1:0] out_10
);

  wire ALUScr, ALUSRC_ID, and_1_out, and_2_out, Branch, BRANCH_ID, CLK, FORW_MEM, IGUAIS, IGUAIS_ID, MemRead,
       MEMREAD_ID, MemtoReg, MEMTOREG_ID, MEMTOREG_MEM, MemWrite, MEMWRITE_ID, MREAD_EX, MTOREG_EX,
       MWRITE_EX, RegWrite, REGWRITE_EX, REGWRITE_ID, REGWRITE_MEM, W;
  wire [1:0] ALUOp, ALUOP_ID;
  wire [2:0] F3_ID, Funct3;
  wire [3:0] alucontrol_1_bit0;
  wire [4:0] A, C, RD_EX, RD_ID, RD_MEM, RS1_ID, RS2_EX, RS2_ID;
  wire [6:0] F7_ID, Funct7, if_id_1_s_ins_if, multiplexer_1_out;
  wire [7:0] multiplexer_5_out;
  wire [31:0] banco_de_registradores_1_sa, banco_de_registradores_1_sb, ex_mem_1_s_r2_ex, id_ex_1_s_imm_id,
       IMM, MEM_DATA, mem_wb_1_s_alu_mem, mem_wb_1_s_read_data_mem, multiplexer_2_out, multiplexer_3_out,
       multiplexer_4_out, multiplexer_7_out, multiplexer_8_out, multiplexer_9_out, multiplexer_10_out, PC,
       RB_ID, rom_1_data, S_PC_IF, shifter_1_out, somador_1_out_3, somador_2_out_3, ULA_ID;

  Clock clock_1 (.out(CLK));
  Registrador_32bits u_PC (.W0(W), .CLK(CLK), .R(R), .D(multiplexer_9_out), .S(PC));
  ROM #(.addrWidth(24), .dataWidth(32), .misaligned("true")) rom_1 (.addr(PC[23:0]), .data(rom_1_data));
  Somador somador_1 (.A(PC), .B(32'h1), .out_3(somador_1_out_3));
  IF_ID if_id_1 (
    .CLK(CLK), .D_PC(PC), .D_INS(rom_1_data), .W(W), .R(R), .S_PC_IF(S_PC_IF),
    .S_INS_IF({Funct7, out_6, A, Funct3, C, if_id_1_s_ins_if}));  // open: DEU_BRANCH, DEU_BRANCH_ID
  and and_1 (and_1_out, BRANCH_ID, IGUAIS_ID);
  HazardDetectionUnit hazarddetectionunit_1 (
    .MEM_WRITE(MemWrite), .IDEXMemRead(MEMREAD_ID), .IFIDRegisterRs(A), .IDEXRegisterRD(RD_ID),
    .IFIDRegisterRt(out_6), .S(W));
  Multiplexer #(.width(7)) multiplexer_1 (
    .in0(if_id_1_s_ins_if), .in1({7{1'b0}}), .out(multiplexer_1_out), .sel(and_1_out));
  ROM #(.addrWidth(7)) Control (
    .addr(multiplexer_1_out), .data({RegWrite, ALUScr, MemWrite, ALUOp, MemtoReg, MemRead, Branch}));
  Multiplexer #(.width(32)) multiplexer_2 (.in0(out_4), .in1(MEM_DATA), .out(multiplexer_2_out), .sel(MREAD_EX));
  ImediateGenerator imediategenerator_1 (
    .in_1({Funct7, out_6, A, Funct3, C, if_id_1_s_ins_if}), .Opcode(multiplexer_1_out), .S(IMM));
  Banco_de_Registradores banco_de_registradores_1 (
    .D(out_3), .R(R), .A(A), .B(out_6), .Clk(CLK), .W(REGWRITE_MEM), .C(RD_MEM),
    .SA(banco_de_registradores_1_sa), .SB(banco_de_registradores_1_sb));
  Forwarding_beq forwarding_beq_1 (
    .RegWrite_ID(REGWRITE_ID), .RD_ID(RD_ID), .MEM_RegisterRD(RD_MEM), .RS2(out_6),
    .EX_RegWrite(REGWRITE_EX), .EX_RegisterRD(RD_EX), .RS1(A), .MEM_RegWrite(REGWRITE_MEM), .ForwardA(out_7),
    .ForwardB(out_10));
  Multiplexer #(.select(2), .width(32)) multiplexer_3 (
    .in0(banco_de_registradores_1_sa), .in1(out_3), .in2(multiplexer_2_out), .in3(ULA_ID),
    .out(multiplexer_3_out), .sel(out_7));
  Multiplexer #(.select(2), .width(32)) multiplexer_4 (
    .in0(banco_de_registradores_1_sb), .in1(out_3), .in2(multiplexer_2_out), .in3(ULA_ID),
    .out(multiplexer_4_out), .sel(out_10));
  Comparator #(.width(32)) comparator_1 (.a(multiplexer_3_out), .b(multiplexer_4_out), .eq(IGUAIS));  // open: gt, lt
  Multiplexer #(.width(8)) multiplexer_5 (
    .in0({8{1'b0}}), .in1({RegWrite, ALUOp, Branch, ALUScr, MemWrite, MemtoReg, MemRead}),
    .out(multiplexer_5_out), .sel(W));
  D_Flip_Flop d_ff_1 (.D(IGUAIS), .clk(CLK), .Q(IGUAIS_ID), .reset(R));  // open: Qn, preset
  UC_ID_EX uc_id_ex_1 (
    .UC_ALUOP(multiplexer_5_out[6:5]), .MEMWRITE(multiplexer_5_out[2]), .CLK(CLK), .R(R),
    .MEMTOREG(multiplexer_5_out[1]), .MEMREAD(multiplexer_5_out[0]), .UC_BRANCH(multiplexer_5_out[4]),
    .UC_ALUSRC(multiplexer_5_out[3]), .REGWRITE(multiplexer_5_out[7]), .S_MEMREAD_ID(MEMREAD_ID),
    .S_MEMTOREG_ID(MEMTOREG_ID), .S_ALUOP_ID(ALUOP_ID), .S_REGWRITE_ID(REGWRITE_ID), .S_ALUSRC_ID(ALUSRC_ID),
    .S_BRANCH_ID(BRANCH_ID), .S_MEMWRITE_ID(MEMWRITE_ID));
  ID_EX id_ex_1 (
    .RD(C), .CLK(CLK), .W(1'b1), .R(R), .RS1_5BITS(A), .RS2_5BITS(out_6), .IMM(IMM), .Funct7(Funct7),
    .FUNCT3(Funct3), .PC(S_PC_IF), .Rb(multiplexer_4_out), .Ra(multiplexer_3_out), .S_RD_ID(RD_ID),
    .S_RS1_ID(RS1_ID), .S_RS2_ID(RS2_ID), .S_Ra_ID(out_2), .S_Rb_ID(RB_ID), .S_IMM_ID(id_ex_1_s_imm_id),
    .FUNCT3_ID(F3_ID));  // open: S_Funct7, S_PC_ID
  Shifter #(.shift("lr"), .width(32)) shifter_1 (.in(IMM), .\dist (5'b00010), .out(shifter_1_out));
  Multiplexer #(.width(32)) multiplexer_6 (.in0(RB_ID), .in1(id_ex_1_s_imm_id), .out(out_8), .sel(ALUSRC_ID));
  Multiplexer #(.select(2), .width(32)) multiplexer_7 (
    .in0(out_2), .in1(out_3), .in2(out_4), .out(multiplexer_7_out), .sel(out_5));  // open: in3
  Multiplexer #(.select(2), .width(32)) multiplexer_8 (
    .in0(out_8), .in1(out_3), .in2(out_4), .out(multiplexer_8_out), .sel(out_9));  // open: in3
  AluControl alucontrol_1 (
    .AluOP(ALUOP_ID), .Func7(F7_ID), .Func3(F3_ID), .Bit0(alucontrol_1_bit0[0]), .Bit1(alucontrol_1_bit0[1]),
    .Bit2(alucontrol_1_bit0[2]), .Bit3(alucontrol_1_bit0[3]));
  Somador somador_2 (.A(shifter_1_out), .B(S_PC_IF), .out_3(somador_2_out_3));
  ULA ula_1 (.Func(alucontrol_1_bit0), .B(multiplexer_8_out), .A(multiplexer_7_out), .S(ULA_ID));  // open: zero
  and and_2 (and_2_out, Branch, IGUAIS);
  UC_EX_MEM uc_ex_mem_1 (
    .REGWRITE_ID(REGWRITE_ID), .R(R), .CLK(CLK), .MEMWRITE_EX(MEMWRITE_ID), .MEMTOREG_EX(MEMTOREG_ID),
    .MEMREAD_EX(MEMREAD_ID), .S_REGWRITE_EX(REGWRITE_EX), .S_MEMWRITE_EX(MWRITE_EX), .S_MEMREAD_EX(MREAD_EX),
    .S_MEMTOREG_EX(MTOREG_EX));  // open: BRANCH, BRANCH_EX
  EX_MEM ex_mem_1 (
    .RS2_ID(RS2_ID), .RD_ID(RD_ID), .R2(RB_ID), .ULA(ULA_ID), .R(R), .W(1'b1), .CLK(CLK), .S_RS2_EX(RS2_EX),
    .RD_EX(RD_EX), .S_ULA_EX(out_4), .S_R2_EX(ex_mem_1_s_r2_ex));  // open: ZERO_VER, SOMADOR, S_SOMADOR_EX, S_ZERO_VER_EX
  forwarding_unit forwarding_unit_1 (
    .ALUSRC(ALUSRC_ID), .MEM_RegisterRD(RD_MEM), .ID_RegisterRT(RS2_ID), .EX_RegWrite(REGWRITE_EX),
    .EX_RegisterRD(RD_EX), .ID_RegisterRS(RS1_ID), .MEM_RegWrite(REGWRITE_MEM), .ForwardB(out_9),
    .ForwardA(out_5));
  Multiplexer #(.width(32)) multiplexer_9 (
    .in0(somador_1_out_3), .in1(somador_2_out_3), .out(multiplexer_9_out), .sel(and_2_out));
  RAM #(.addrWidth(24), .dataWidth(32)) ram_1 (
    .addr(out_4[23:0]), .we(MWRITE_EX), .oe(MREAD_EX), .clk(CLK), .din(multiplexer_10_out), .dout(MEM_DATA));
  Multiplexer #(.width(32)) multiplexer_10 (
    .in0(ex_mem_1_s_r2_ex), .in1(out_3), .out(multiplexer_10_out), .sel(FORW_MEM));
  UC_MEM_WB uc_mem_wb_1 (
    .R(R), .REGWRITE_EX(REGWRITE_EX), .WB_EX(MTOREG_EX), .CLK(CLK), .S_REGWRITE_MEM(REGWRITE_MEM),
    .WB_MEM(MEMTOREG_MEM));
  MEM_WB mem_wb_1 (
    .ALU(out_4), .READ_DATA(MEM_DATA), .RD_EX(RD_EX), .W(1'b1), .R(R), .CLK(CLK), .RD_MEM(RD_MEM),
    .S_READ_DATA_MEM(mem_wb_1_s_read_data_mem), .S_ALU_MEM(mem_wb_1_s_alu_mem));
  Forwarding_MEM forwarding_mem_1 (
    .REGWRITE_MEM(REGWRITE_MEM), .MEMWRITE_EX(MWRITE_EX), .RD_MEM(RD_MEM), .R2_EX(RS2_EX),
    .Forwading(FORW_MEM));
  Multiplexer #(.width(32)) multiplexer_11 (
    .in0(mem_wb_1_s_alu_mem), .in1(mem_wb_1_s_read_data_mem), .out(out_3), .sel(MEMTOREG_MEM));
  ID_EX id_ex_2 ();  // open: RD, CLK, W, R, RS1_5BITS, RS2_5BITS, IMM, Funct7, FUNCT3, PC, Rb, Ra, S_RD_ID, S_Funct7, S_RS1_ID, S_RS2_ID, S_PC_ID, S_Ra_ID, S_Rb_ID, S_IMM_ID, FUNCT3_ID

  // Other names for the same wires on the sheet: ULA_EX[31:0] = out_4; B[4:0] = out_6; FOR_A[1:0] = out_7;
  //   FOR_B[1:0] = out_10; FORW_A[1:0] = out_5; FORW_B[1:0] = out_9; RA_ID[31:0] = out_2

  // Notes on the sheet:
  //   contents of rom_1 (hex, n*v repeats v):
  //   a00093 2103 110a63
  //   contents of Control (hex, n*v repeats v):
  //   0 0 0 c6 15*0 d0 15*0 60 15*0 90 47*0 9
endmodule

module Banco_de_Registradores (
  input  [31:0] D,
  input  R,
  input  Clk,
  input  [4:0] A,
  input  W,
  input  [4:0] C,
  input  [4:0] B,
  output [31:0] SA,
  output [31:0] SB
);

  wire demultiplexer_1_out1, demultiplexer_1_out2, demultiplexer_1_out3, demultiplexer_1_out4,
       demultiplexer_1_out5, demultiplexer_1_out6, demultiplexer_1_out7, demultiplexer_1_out8,
       demultiplexer_1_out9, demultiplexer_1_out10, demultiplexer_1_out11, demultiplexer_1_out12,
       demultiplexer_1_out13, demultiplexer_1_out14, demultiplexer_1_out15, demultiplexer_1_out16,
       demultiplexer_1_out17, demultiplexer_1_out18, demultiplexer_1_out19, demultiplexer_1_out20,
       demultiplexer_1_out21, demultiplexer_1_out22, demultiplexer_1_out23, demultiplexer_1_out24,
       demultiplexer_1_out25, demultiplexer_1_out26, demultiplexer_1_out27, demultiplexer_1_out28,
       demultiplexer_1_out29, demultiplexer_1_out30, demultiplexer_1_out31;
  wire [31:0] registrador_32bits_1_s, registrador_32bits_2_s, registrador_32bits_3_s, registrador_32bits_4_s,
       registrador_32bits_5_s, registrador_32bits_6_s, registrador_32bits_7_s, registrador_32bits_8_s,
       registrador_32bits_9_s, registrador_32bits_10_s, registrador_32bits_11_s, registrador_32bits_12_s,
       registrador_32bits_13_s, registrador_32bits_14_s, registrador_32bits_15_s, registrador_32bits_16_s,
       registrador_32bits_17_s, registrador_32bits_18_s, registrador_32bits_19_s, registrador_32bits_20_s,
       registrador_32bits_21_s, registrador_32bits_22_s, registrador_32bits_23_s, registrador_32bits_24_s,
       registrador_32bits_25_s, registrador_32bits_26_s, registrador_32bits_27_s, registrador_32bits_28_s,
       registrador_32bits_29_s, registrador_32bits_30_s, registrador_32bits_31_s, registrador_32bits_32_s;

  Demultiplexer #(.select(5)) demultiplexer_1 (
    .out1(demultiplexer_1_out1), .out2(demultiplexer_1_out2), .out3(demultiplexer_1_out3),
    .out4(demultiplexer_1_out4), .out5(demultiplexer_1_out5), .out6(demultiplexer_1_out6),
    .out7(demultiplexer_1_out7), .out8(demultiplexer_1_out8), .out9(demultiplexer_1_out9),
    .out10(demultiplexer_1_out10), .out11(demultiplexer_1_out11), .out12(demultiplexer_1_out12),
    .out13(demultiplexer_1_out13), .out14(demultiplexer_1_out14), .out15(demultiplexer_1_out15),
    .out16(demultiplexer_1_out16), .out17(demultiplexer_1_out17), .out18(demultiplexer_1_out18),
    .out19(demultiplexer_1_out19), .out20(demultiplexer_1_out20), .out21(demultiplexer_1_out21),
    .out22(demultiplexer_1_out22), .out23(demultiplexer_1_out23), .out24(demultiplexer_1_out24),
    .out25(demultiplexer_1_out25), .out26(demultiplexer_1_out26), .out27(demultiplexer_1_out27),
    .out28(demultiplexer_1_out28), .out29(demultiplexer_1_out29), .out30(demultiplexer_1_out30),
    .out31(demultiplexer_1_out31), .in(W), .sel(C));  // open: out0
  Registrador_32bits registrador_32bits_1 (.W0(1'b1), .D({32{1'b0}}), .S(registrador_32bits_1_s));  // open: CLK, R
  Registrador_32bits registrador_32bits_2 (
    .W0(demultiplexer_1_out1), .CLK(Clk), .R(R), .D(D), .S(registrador_32bits_2_s));
  Registrador_32bits registrador_32bits_3 (
    .W0(demultiplexer_1_out2), .CLK(Clk), .R(R), .D(D), .S(registrador_32bits_3_s));
  Registrador_32bits registrador_32bits_4 (
    .W0(demultiplexer_1_out3), .CLK(Clk), .R(R), .D(D), .S(registrador_32bits_4_s));
  Registrador_32bits registrador_32bits_5 (
    .W0(demultiplexer_1_out4), .CLK(Clk), .R(R), .D(D), .S(registrador_32bits_5_s));
  Registrador_32bits registrador_32bits_6 (
    .W0(demultiplexer_1_out5), .CLK(Clk), .R(R), .D(D), .S(registrador_32bits_6_s));
  Registrador_32bits registrador_32bits_7 (
    .W0(demultiplexer_1_out7), .CLK(Clk), .R(R), .D(D), .S(registrador_32bits_7_s));
  Registrador_32bits registrador_32bits_8 (
    .W0(demultiplexer_1_out8), .CLK(Clk), .R(R), .D(D), .S(registrador_32bits_8_s));
  Registrador_32bits registrador_32bits_9 (
    .W0(demultiplexer_1_out9), .CLK(Clk), .R(R), .D(D), .S(registrador_32bits_9_s));
  Registrador_32bits registrador_32bits_10 (
    .W0(demultiplexer_1_out10), .CLK(Clk), .R(R), .D(D), .S(registrador_32bits_10_s));
  Registrador_32bits registrador_32bits_11 (
    .W0(demultiplexer_1_out11), .CLK(Clk), .R(R), .D(D), .S(registrador_32bits_11_s));
  Registrador_32bits registrador_32bits_12 (
    .W0(demultiplexer_1_out12), .CLK(Clk), .R(R), .D(D), .S(registrador_32bits_12_s));
  Registrador_32bits registrador_32bits_13 (
    .W0(demultiplexer_1_out13), .CLK(Clk), .R(R), .D(D), .S(registrador_32bits_13_s));
  Registrador_32bits registrador_32bits_14 (
    .W0(demultiplexer_1_out14), .CLK(Clk), .R(R), .D(D), .S(registrador_32bits_14_s));
  Registrador_32bits registrador_32bits_15 (
    .W0(demultiplexer_1_out15), .CLK(Clk), .R(R), .D(D), .S(registrador_32bits_15_s));
  Registrador_32bits registrador_32bits_16 (
    .W0(demultiplexer_1_out16), .CLK(Clk), .R(R), .D(D), .S(registrador_32bits_16_s));
  Registrador_32bits registrador_32bits_17 (
    .W0(demultiplexer_1_out17), .CLK(Clk), .R(R), .D(D), .S(registrador_32bits_17_s));
  Registrador_32bits registrador_32bits_18 (
    .W0(demultiplexer_1_out18), .CLK(Clk), .R(R), .D(D), .S(registrador_32bits_18_s));
  Registrador_32bits registrador_32bits_19 (
    .W0(demultiplexer_1_out19), .CLK(Clk), .R(R), .D(D), .S(registrador_32bits_19_s));
  Registrador_32bits registrador_32bits_20 (
    .W0(demultiplexer_1_out20), .CLK(Clk), .R(R), .D(D), .S(registrador_32bits_20_s));
  Registrador_32bits registrador_32bits_21 (
    .W0(demultiplexer_1_out21), .CLK(Clk), .R(R), .D(D), .S(registrador_32bits_21_s));
  Registrador_32bits registrador_32bits_22 (
    .W0(demultiplexer_1_out22), .CLK(Clk), .R(R), .D(D), .S(registrador_32bits_22_s));
  Registrador_32bits registrador_32bits_23 (
    .W0(demultiplexer_1_out23), .CLK(Clk), .R(R), .D(D), .S(registrador_32bits_23_s));
  Registrador_32bits registrador_32bits_24 (
    .W0(demultiplexer_1_out24), .CLK(Clk), .R(R), .D(D), .S(registrador_32bits_24_s));
  Registrador_32bits registrador_32bits_25 (
    .W0(demultiplexer_1_out25), .CLK(Clk), .R(R), .D(D), .S(registrador_32bits_25_s));
  Registrador_32bits registrador_32bits_26 (
    .W0(demultiplexer_1_out26), .CLK(Clk), .R(R), .D(D), .S(registrador_32bits_26_s));
  Registrador_32bits registrador_32bits_27 (
    .W0(demultiplexer_1_out27), .CLK(Clk), .R(R), .D(D), .S(registrador_32bits_27_s));
  Registrador_32bits registrador_32bits_28 (
    .W0(demultiplexer_1_out28), .CLK(Clk), .R(R), .D(D), .S(registrador_32bits_28_s));
  Registrador_32bits registrador_32bits_29 (
    .W0(demultiplexer_1_out29), .CLK(Clk), .R(R), .D(D), .S(registrador_32bits_29_s));
  Registrador_32bits registrador_32bits_30 (
    .W0(demultiplexer_1_out30), .CLK(Clk), .R(R), .D(D), .S(registrador_32bits_30_s));
  Registrador_32bits registrador_32bits_31 (
    .W0(demultiplexer_1_out31), .CLK(Clk), .R(R), .D(D), .S(registrador_32bits_31_s));
  Registrador_32bits registrador_32bits_32 (
    .W0(demultiplexer_1_out6), .CLK(Clk), .R(R), .D(D), .S(registrador_32bits_32_s));
  Multiplexer #(.select(5), .width(32)) multiplexer_1 (
    .in0(registrador_32bits_1_s), .in1(registrador_32bits_2_s), .in2(registrador_32bits_3_s),
    .in3(registrador_32bits_4_s), .in4(registrador_32bits_5_s), .in5(registrador_32bits_6_s),
    .in6(registrador_32bits_32_s), .in7(registrador_32bits_7_s), .in8(registrador_32bits_8_s),
    .in9(registrador_32bits_9_s), .in10(registrador_32bits_10_s), .in11(registrador_32bits_11_s),
    .in12(registrador_32bits_12_s), .in13(registrador_32bits_13_s), .in14(registrador_32bits_14_s),
    .in15(registrador_32bits_15_s), .in16(registrador_32bits_16_s), .in17(registrador_32bits_17_s),
    .in18(registrador_32bits_18_s), .in19(registrador_32bits_19_s), .in20(registrador_32bits_20_s),
    .in21(registrador_32bits_21_s), .in22(registrador_32bits_22_s), .in23(registrador_32bits_23_s),
    .in24(registrador_32bits_24_s), .in25(registrador_32bits_25_s), .in26(registrador_32bits_26_s),
    .in27(registrador_32bits_27_s), .in28(registrador_32bits_28_s), .in29(registrador_32bits_29_s),
    .in30(registrador_32bits_30_s), .in31(registrador_32bits_31_s), .out(SA), .sel(A));
  Multiplexer #(.select(5), .width(32)) multiplexer_2 (
    .in0(registrador_32bits_1_s), .in1(registrador_32bits_2_s), .in2(registrador_32bits_3_s),
    .in3(registrador_32bits_4_s), .in4(registrador_32bits_5_s), .in5(registrador_32bits_6_s),
    .in6(registrador_32bits_32_s), .in7(registrador_32bits_7_s), .in8(registrador_32bits_8_s),
    .in9(registrador_32bits_9_s), .in10(registrador_32bits_10_s), .in11(registrador_32bits_11_s),
    .in12(registrador_32bits_12_s), .in13(registrador_32bits_13_s), .in14(registrador_32bits_14_s),
    .in15(registrador_32bits_15_s), .in16(registrador_32bits_16_s), .in17(registrador_32bits_17_s),
    .in18(registrador_32bits_18_s), .in19(registrador_32bits_19_s), .in20(registrador_32bits_20_s),
    .in21(registrador_32bits_21_s), .in22(registrador_32bits_22_s), .in23(registrador_32bits_23_s),
    .in24(registrador_32bits_24_s), .in25(registrador_32bits_25_s), .in26(registrador_32bits_26_s),
    .in27(registrador_32bits_27_s), .in28(registrador_32bits_28_s), .in29(registrador_32bits_29_s),
    .in30(registrador_32bits_30_s), .in31(registrador_32bits_31_s), .out(SB), .sel(B));
endmodule

module Registrador_32bits (
  input  W0,
  input  CLK,
  input  R,
  input  [31:0] D,
  output [31:0] S
);

  Registrador_4bits registrador_4bits_1 (.CLK(CLK), .W0(W0), .R(R), .D0(D[3:0]), .S(S[3:0]));
  Registrador_4bits registrador_4bits_2 (.CLK(CLK), .W0(W0), .R(R), .D0(D[7:4]), .S(S[7:4]));
  Registrador_4bits registrador_4bits_3 (.CLK(CLK), .W0(W0), .R(R), .D0(D[11:8]), .S(S[11:8]));
  Registrador_4bits registrador_4bits_4 (.CLK(CLK), .W0(W0), .R(R), .D0(D[15:12]), .S(S[15:12]));
  Registrador_4bits registrador_4bits_5 (.CLK(CLK), .W0(W0), .R(R), .D0(D[19:16]), .S(S[19:16]));
  Registrador_4bits registrador_4bits_6 (.CLK(CLK), .W0(W0), .R(R), .D0(D[23:20]), .S(S[23:20]));
  Registrador_4bits registrador_4bits_7 (.CLK(CLK), .W0(W0), .R(R), .D0(D[27:24]), .S(S[27:24]));
  Registrador_4bits registrador_4bits_8 (.CLK(CLK), .W0(W0), .R(R), .D0(D[31:28]), .S(S[31:28]));
endmodule

module Registrador_4bits (
  input  CLK,
  input  W0,
  input  R,
  input  [3:0] D0,
  output [3:0] S
);

  wire multiplexer_1_out, multiplexer_2_out, multiplexer_3_out, multiplexer_4_out;

  Multiplexer multiplexer_1 (.in0(S[0]), .in1(D0[0]), .out(multiplexer_1_out), .sel(W0));
  Multiplexer multiplexer_2 (.in0(S[1]), .in1(D0[1]), .out(multiplexer_2_out), .sel(W0));
  Multiplexer multiplexer_3 (.in0(S[2]), .in1(D0[2]), .out(multiplexer_3_out), .sel(W0));
  Multiplexer multiplexer_4 (.in0(S[3]), .in1(D0[3]), .out(multiplexer_4_out), .sel(W0));
  D_Flip_Flop d_ff_1 (.D(multiplexer_1_out), .clk(CLK), .Q(S[0]), .reset(R));  // open: Qn, preset
  D_Flip_Flop d_ff_2 (.D(multiplexer_2_out), .clk(CLK), .Q(S[1]), .reset(R));  // open: Qn, preset
  D_Flip_Flop d_ff_3 (.D(multiplexer_3_out), .clk(CLK), .Q(S[2]), .reset(R));  // open: Qn, preset
  D_Flip_Flop d_ff_4 (.D(multiplexer_4_out), .clk(CLK), .Q(S[3]), .reset(R));  // open: Qn, preset
endmodule

module ULA (
  input  [31:0] B,
  input  [31:0] A,
  input  [3:0] Func,
  output [31:0] S,
  output zero
);

  wire [31:0] and_1_out, or_1_out, shifter_1_out, somador_1_out_3, subtrador_1_out_3, xnor_1_out;

  Shifter #(.width(32)) shifter_1 (.in(A), .\dist (B[4:0]), .out(shifter_1_out));
  assign and_1_out = A & B;  // AND_Gate and_1, 32 bits wide
  assign or_1_out = A | B;  // OR_Gate or_1, 32 bits wide
  Somador somador_1 (.A(A), .B(B), .out_3(somador_1_out_3));
  Subtrador subtrador_1 (.A(A), .B(B), .out_3(subtrador_1_out_3));
  assign xnor_1_out = ~(A ^ B);  // XNOR_Gate xnor_1, 32 bits wide
  Multiplexer #(.select(4), .width(32)) multiplexer_1 (
    .in0(and_1_out), .in1(or_1_out), .in2(somador_1_out_3), .in4(xnor_1_out), .in5(shifter_1_out),
    .in6(subtrador_1_out_3), .out(S), .sel(Func));  // open: in3, in7, in8, in9, in10, in11, in12, in13, in14, in15
  Zeroverifyer zeroverifyer_1 (.in_1(S), .out_2(zero));
endmodule

module full_adder (
  input  A,
  input  B,
  input  Cin,
  output S,
  output Cout
);

  wire and_1_out, and_2_out, and_3_out, xor_1_out;

  xor xor_1 (xor_1_out, B, Cin);
  and and_1 (and_1_out, Cin, B);
  and and_2 (and_2_out, Cin, A);
  and and_3 (and_3_out, B, A);
  xor xor_2 (S, A, xor_1_out);
  or or_1 (Cout, and_1_out, and_2_out, and_3_out);
endmodule

module half_adder (
  input  A,
  input  B,
  output S,
  output Cout
);

  xor xor_1 (S, A, B);
  and and_1 (Cout, A, B);
endmodule

module Somador (
  input  [31:0] A,
  input  [31:0] B,
  output [31:0] out_3
);

  wire full_adder_1_cout, full_adder_2_cout, full_adder_3_cout, full_adder_4_cout, full_adder_5_cout,
       full_adder_6_cout, full_adder_7_cout, full_adder_8_cout, full_adder_9_cout, full_adder_10_cout,
       full_adder_11_cout, full_adder_12_cout, full_adder_13_cout, full_adder_14_cout, full_adder_15_cout,
       full_adder_16_cout, full_adder_17_cout, full_adder_18_cout, full_adder_19_cout, full_adder_20_cout,
       full_adder_21_cout, full_adder_22_cout, full_adder_23_cout, full_adder_24_cout, full_adder_25_cout,
       full_adder_26_cout, full_adder_27_cout, full_adder_28_cout, full_adder_29_cout, full_adder_30_cout,
       half_adder_1_cout;

  half_adder half_adder_1 (.A(A[0]), .B(B[0]), .S(out_3[0]), .Cout(half_adder_1_cout));
  full_adder full_adder_1 (.A(A[1]), .B(B[1]), .Cin(half_adder_1_cout), .S(out_3[1]), .Cout(full_adder_1_cout));
  full_adder full_adder_2 (.A(A[2]), .B(B[2]), .Cin(full_adder_1_cout), .S(out_3[2]), .Cout(full_adder_2_cout));
  full_adder full_adder_3 (.A(A[3]), .B(B[3]), .Cin(full_adder_2_cout), .S(out_3[3]), .Cout(full_adder_3_cout));
  full_adder full_adder_4 (.A(A[4]), .B(B[4]), .Cin(full_adder_3_cout), .S(out_3[4]), .Cout(full_adder_4_cout));
  full_adder full_adder_5 (.A(A[5]), .B(B[5]), .Cin(full_adder_4_cout), .S(out_3[5]), .Cout(full_adder_5_cout));
  full_adder full_adder_6 (.A(A[6]), .B(B[6]), .Cin(full_adder_5_cout), .S(out_3[6]), .Cout(full_adder_6_cout));
  full_adder full_adder_7 (.A(A[7]), .B(B[7]), .Cin(full_adder_6_cout), .S(out_3[7]), .Cout(full_adder_7_cout));
  full_adder full_adder_8 (.A(A[8]), .B(B[8]), .Cin(full_adder_7_cout), .S(out_3[8]), .Cout(full_adder_8_cout));
  full_adder full_adder_9 (.A(A[9]), .B(B[9]), .Cin(full_adder_8_cout), .S(out_3[9]), .Cout(full_adder_9_cout));
  full_adder full_adder_10 (.A(A[10]), .B(B[10]), .Cin(full_adder_9_cout), .S(out_3[10]), .Cout(full_adder_10_cout));
  full_adder full_adder_11 (.A(A[11]), .B(B[11]), .Cin(full_adder_10_cout), .S(out_3[11]), .Cout(full_adder_11_cout));
  full_adder full_adder_12 (.A(A[12]), .B(B[12]), .Cin(full_adder_11_cout), .S(out_3[12]), .Cout(full_adder_12_cout));
  full_adder full_adder_13 (.A(A[13]), .B(B[13]), .Cin(full_adder_12_cout), .S(out_3[13]), .Cout(full_adder_13_cout));
  full_adder full_adder_14 (.A(A[14]), .B(B[14]), .Cin(full_adder_13_cout), .S(out_3[14]), .Cout(full_adder_14_cout));
  full_adder full_adder_15 (.A(A[15]), .B(B[15]), .Cin(full_adder_14_cout), .S(out_3[15]), .Cout(full_adder_15_cout));
  full_adder full_adder_16 (.A(A[16]), .B(B[16]), .Cin(full_adder_15_cout), .S(out_3[16]), .Cout(full_adder_16_cout));
  full_adder full_adder_17 (.A(A[17]), .B(B[17]), .Cin(full_adder_16_cout), .S(out_3[17]), .Cout(full_adder_17_cout));
  full_adder full_adder_18 (.A(A[18]), .B(B[18]), .Cin(full_adder_17_cout), .S(out_3[18]), .Cout(full_adder_18_cout));
  full_adder full_adder_19 (.A(A[19]), .B(B[19]), .Cin(full_adder_18_cout), .S(out_3[19]), .Cout(full_adder_19_cout));
  full_adder full_adder_20 (.A(A[20]), .B(B[20]), .Cin(full_adder_19_cout), .S(out_3[20]), .Cout(full_adder_20_cout));
  full_adder full_adder_21 (.A(A[21]), .B(B[21]), .Cin(full_adder_20_cout), .S(out_3[21]), .Cout(full_adder_21_cout));
  full_adder full_adder_22 (.A(A[22]), .B(B[22]), .Cin(full_adder_21_cout), .S(out_3[22]), .Cout(full_adder_22_cout));
  full_adder full_adder_23 (.A(A[23]), .B(B[23]), .Cin(full_adder_22_cout), .S(out_3[23]), .Cout(full_adder_23_cout));
  full_adder full_adder_24 (.A(A[24]), .B(B[24]), .Cin(full_adder_23_cout), .S(out_3[24]), .Cout(full_adder_24_cout));
  full_adder full_adder_25 (.A(A[25]), .B(B[25]), .Cin(full_adder_24_cout), .S(out_3[25]), .Cout(full_adder_25_cout));
  full_adder full_adder_26 (.A(A[26]), .B(B[26]), .Cin(full_adder_25_cout), .S(out_3[26]), .Cout(full_adder_26_cout));
  full_adder full_adder_27 (.A(A[27]), .B(B[27]), .Cin(full_adder_26_cout), .S(out_3[27]), .Cout(full_adder_27_cout));
  full_adder full_adder_28 (.A(A[28]), .B(B[28]), .Cin(full_adder_27_cout), .S(out_3[28]), .Cout(full_adder_28_cout));
  full_adder full_adder_29 (.A(A[29]), .B(B[29]), .Cin(full_adder_28_cout), .S(out_3[29]), .Cout(full_adder_29_cout));
  full_adder full_adder_30 (.A(A[30]), .B(B[30]), .Cin(full_adder_29_cout), .S(out_3[30]), .Cout(full_adder_30_cout));
  full_adder full_adder_31 (.A(A[31]), .B(B[31]), .Cin(full_adder_30_cout), .S(out_3[31]));  // open: Cout

  // Other names for the same wires on the sheet: S0 = out_3[0]; S1 = out_3[1]; S2 = out_3[2]; S3 = out_3[3];
  //   S4 = out_3[4]; S5 = out_3[5]; S6 = out_3[6]; S7 = out_3[7]; S8 = out_3[8]; S9 = out_3[9]; S10 = out_3[10];
  //   S11 = out_3[11]; S12 = out_3[12]; S13 = out_3[13]; S14 = out_3[14]; S15 = out_3[15]; S16 = out_3[16];
  //   S17 = out_3[17]; S18 = out_3[18]; S19 = out_3[19]; S20 = out_3[20]; S21 = out_3[21]; S22 = out_3[22];
  //   S23 = out_3[23]; S24 = out_3[24]; S25 = out_3[25]; S26 = out_3[26]; S27 = out_3[27]; S28 = out_3[28];
  //   S29 = out_3[29]; S30 = out_3[30]; S31 = out_3[31]
endmodule

module somador_cmpl2 (
  input  [31:0] in_1,
  output [31:0] out_2
);

  wire B0, B1, B2, B3, B4, B5, B6, B7, B8, B9, B10, B11, B12, B13, B14, B15, B16, B17, B18, B19, B20, B21,
       B22, B23, B24, B25, B26, B27, B28, B29, B30, B31, half_adder_1_cout, half_adder_2_cout,
       half_adder_3_cout, half_adder_4_cout, half_adder_5_cout, half_adder_6_cout, half_adder_7_cout,
       half_adder_8_cout, half_adder_9_cout, half_adder_10_cout, half_adder_11_cout, half_adder_12_cout,
       half_adder_13_cout, half_adder_14_cout, half_adder_15_cout, half_adder_16_cout, half_adder_17_cout,
       half_adder_18_cout, half_adder_19_cout, half_adder_20_cout, half_adder_21_cout, half_adder_22_cout,
       half_adder_23_cout, half_adder_24_cout, half_adder_25_cout, half_adder_26_cout, half_adder_27_cout,
       half_adder_28_cout, half_adder_29_cout, half_adder_30_cout, half_adder_31_cout;

  not not_1 (B0, in_1[0]);
  not not_2 (B1, in_1[1]);
  not not_3 (B2, in_1[2]);
  not not_4 (B3, in_1[3]);
  not not_5 (B4, in_1[4]);
  not not_6 (B5, in_1[5]);
  not not_7 (B6, in_1[6]);
  not not_8 (B7, in_1[7]);
  not not_9 (B8, in_1[8]);
  not not_10 (B9, in_1[9]);
  not not_11 (B10, in_1[10]);
  not not_12 (B11, in_1[11]);
  not not_13 (B12, in_1[12]);
  not not_14 (B13, in_1[13]);
  not not_15 (B14, in_1[14]);
  not not_16 (B15, in_1[15]);
  not not_17 (B16, in_1[16]);
  not not_18 (B17, in_1[17]);
  not not_19 (B18, in_1[18]);
  not not_20 (B19, in_1[19]);
  not not_21 (B20, in_1[20]);
  not not_22 (B21, in_1[21]);
  not not_23 (B22, in_1[22]);
  not not_24 (B23, in_1[23]);
  not not_25 (B24, in_1[24]);
  not not_26 (B25, in_1[25]);
  not not_27 (B26, in_1[26]);
  not not_28 (B27, in_1[27]);
  not not_29 (B28, in_1[28]);
  not not_30 (B29, in_1[29]);
  not not_31 (B30, in_1[30]);
  not not_32 (B31, in_1[31]);
  half_adder half_adder_1 (.A(1'b1), .B(B0), .S(out_2[0]), .Cout(half_adder_1_cout));
  half_adder half_adder_2 (.A(B1), .B(half_adder_1_cout), .S(out_2[1]), .Cout(half_adder_2_cout));
  half_adder half_adder_3 (.A(B2), .B(half_adder_2_cout), .S(out_2[2]), .Cout(half_adder_3_cout));
  half_adder half_adder_4 (.A(B3), .B(half_adder_3_cout), .S(out_2[3]), .Cout(half_adder_4_cout));
  half_adder half_adder_5 (.A(B4), .B(half_adder_4_cout), .S(out_2[4]), .Cout(half_adder_5_cout));
  half_adder half_adder_6 (.A(B5), .B(half_adder_5_cout), .S(out_2[5]), .Cout(half_adder_6_cout));
  half_adder half_adder_7 (.A(B6), .B(half_adder_6_cout), .S(out_2[6]), .Cout(half_adder_7_cout));
  half_adder half_adder_8 (.A(B7), .B(half_adder_7_cout), .S(out_2[7]), .Cout(half_adder_8_cout));
  half_adder half_adder_9 (.A(B8), .B(half_adder_8_cout), .S(out_2[8]), .Cout(half_adder_9_cout));
  half_adder half_adder_10 (.A(B9), .B(half_adder_9_cout), .S(out_2[9]), .Cout(half_adder_10_cout));
  half_adder half_adder_11 (.A(B10), .B(half_adder_10_cout), .S(out_2[10]), .Cout(half_adder_11_cout));
  half_adder half_adder_12 (.A(B11), .B(half_adder_11_cout), .S(out_2[11]), .Cout(half_adder_12_cout));
  half_adder half_adder_13 (.A(B12), .B(half_adder_12_cout), .S(out_2[12]), .Cout(half_adder_13_cout));
  half_adder half_adder_14 (.A(B13), .B(half_adder_13_cout), .S(out_2[13]), .Cout(half_adder_14_cout));
  half_adder half_adder_15 (.A(B14), .B(half_adder_14_cout), .S(out_2[14]), .Cout(half_adder_15_cout));
  half_adder half_adder_16 (.A(B15), .B(half_adder_15_cout), .S(out_2[15]), .Cout(half_adder_16_cout));
  half_adder half_adder_17 (.A(B16), .B(half_adder_16_cout), .S(out_2[16]), .Cout(half_adder_17_cout));
  half_adder half_adder_18 (.A(B17), .B(half_adder_17_cout), .S(out_2[17]), .Cout(half_adder_18_cout));
  half_adder half_adder_19 (.A(B18), .B(half_adder_18_cout), .S(out_2[18]), .Cout(half_adder_19_cout));
  half_adder half_adder_20 (.A(B19), .B(half_adder_19_cout), .S(out_2[19]), .Cout(half_adder_20_cout));
  half_adder half_adder_21 (.A(B20), .B(half_adder_20_cout), .S(out_2[20]), .Cout(half_adder_21_cout));
  half_adder half_adder_22 (.A(B21), .B(half_adder_21_cout), .S(out_2[21]), .Cout(half_adder_22_cout));
  half_adder half_adder_23 (.A(B22), .B(half_adder_22_cout), .S(out_2[22]), .Cout(half_adder_23_cout));
  half_adder half_adder_24 (.A(B23), .B(half_adder_23_cout), .S(out_2[23]), .Cout(half_adder_24_cout));
  half_adder half_adder_25 (.A(B24), .B(half_adder_24_cout), .S(out_2[24]), .Cout(half_adder_25_cout));
  half_adder half_adder_26 (.A(B25), .B(half_adder_25_cout), .S(out_2[25]), .Cout(half_adder_26_cout));
  half_adder half_adder_27 (.A(B26), .B(half_adder_26_cout), .S(out_2[26]), .Cout(half_adder_27_cout));
  half_adder half_adder_28 (.A(B27), .B(half_adder_27_cout), .S(out_2[27]), .Cout(half_adder_28_cout));
  half_adder half_adder_29 (.A(B28), .B(half_adder_28_cout), .S(out_2[28]), .Cout(half_adder_29_cout));
  half_adder half_adder_30 (.A(B29), .B(half_adder_29_cout), .S(out_2[29]), .Cout(half_adder_30_cout));
  half_adder half_adder_31 (.A(B30), .B(half_adder_30_cout), .S(out_2[30]), .Cout(half_adder_31_cout));
  half_adder half_adder_32 (.A(B31), .B(half_adder_31_cout), .S(out_2[31]));  // open: Cout

  // Other names for the same wires on the sheet: S0 = out_2[0]; S1 = out_2[1]; S2 = out_2[2]; S3 = out_2[3];
  //   S4 = out_2[4]; S5 = out_2[5]; S6 = out_2[6]; S7 = out_2[7]; S8 = out_2[8]; S9 = out_2[9]; S10 = out_2[10];
  //   S11 = out_2[11]; S12 = out_2[12]; S13 = out_2[13]; S14 = out_2[14]; S15 = out_2[15]; S16 = out_2[16];
  //   S17 = out_2[17]; S18 = out_2[18]; S19 = out_2[19]; S20 = out_2[20]; S21 = out_2[21]; S22 = out_2[22];
  //   S23 = out_2[23]; S24 = out_2[24]; S25 = out_2[25]; S26 = out_2[26]; S27 = out_2[27]; S28 = out_2[28];
  //   S29 = out_2[29]; S30 = out_2[30]; S31 = out_2[31]
endmodule

module Subtrador (
  input  [31:0] A,
  input  [31:0] B,
  output [31:0] out_3
);

  wire B0, B1, B2, B3, B4, B5, B6, B7, B8, B9, B10, B11, B12, B13, B14, B15, B16, B17, B18, B19, B20, B21,
       B22, B23, B24, B25, B26, B27, B28, B29, B30, B31, full_adder_1_cout, full_adder_2_cout,
       full_adder_3_cout, full_adder_4_cout, full_adder_5_cout, full_adder_6_cout, full_adder_7_cout,
       full_adder_8_cout, full_adder_9_cout, full_adder_10_cout, full_adder_11_cout, full_adder_12_cout,
       full_adder_13_cout, full_adder_14_cout, full_adder_15_cout, full_adder_16_cout, full_adder_17_cout,
       full_adder_18_cout, full_adder_19_cout, full_adder_20_cout, full_adder_21_cout, full_adder_22_cout,
       full_adder_23_cout, full_adder_24_cout, full_adder_25_cout, full_adder_26_cout, full_adder_27_cout,
       full_adder_28_cout, full_adder_29_cout, full_adder_30_cout, half_adder_1_cout;

  somador_cmpl2 somador_cmpl2_1 (
    .in_1(B),
    .out_2({B31, B30, B29, B28, B27, B26, B25, B24, B23, B22, B21, B20, B19, B18, B17, B16, B15, B14, B13, B12, B11, B10, B9, B8, B7, B6, B5, B4, B3, B2, B1, B0}));
  half_adder half_adder_1 (.A(A[0]), .B(B0), .S(out_3[0]), .Cout(half_adder_1_cout));
  full_adder full_adder_1 (.A(A[1]), .B(B1), .Cin(half_adder_1_cout), .S(out_3[1]), .Cout(full_adder_1_cout));
  full_adder full_adder_2 (.A(A[2]), .B(B2), .Cin(full_adder_1_cout), .S(out_3[2]), .Cout(full_adder_2_cout));
  full_adder full_adder_3 (.A(A[3]), .B(B3), .Cin(full_adder_2_cout), .S(out_3[3]), .Cout(full_adder_3_cout));
  full_adder full_adder_4 (.A(A[4]), .B(B4), .Cin(full_adder_3_cout), .S(out_3[4]), .Cout(full_adder_4_cout));
  full_adder full_adder_5 (.A(A[5]), .B(B5), .Cin(full_adder_4_cout), .S(out_3[5]), .Cout(full_adder_5_cout));
  full_adder full_adder_6 (.A(A[6]), .B(B6), .Cin(full_adder_5_cout), .S(out_3[6]), .Cout(full_adder_6_cout));
  full_adder full_adder_7 (.A(A[7]), .B(B7), .Cin(full_adder_6_cout), .S(out_3[7]), .Cout(full_adder_7_cout));
  full_adder full_adder_8 (.A(A[8]), .B(B8), .Cin(full_adder_7_cout), .S(out_3[8]), .Cout(full_adder_8_cout));
  full_adder full_adder_9 (.A(A[9]), .B(B9), .Cin(full_adder_8_cout), .S(out_3[9]), .Cout(full_adder_9_cout));
  full_adder full_adder_10 (.A(A[10]), .B(B10), .Cin(full_adder_9_cout), .S(out_3[10]), .Cout(full_adder_10_cout));
  full_adder full_adder_11 (.A(A[11]), .B(B11), .Cin(full_adder_10_cout), .S(out_3[11]), .Cout(full_adder_11_cout));
  full_adder full_adder_12 (.A(A[12]), .B(B12), .Cin(full_adder_11_cout), .S(out_3[12]), .Cout(full_adder_12_cout));
  full_adder full_adder_13 (.A(A[13]), .B(B13), .Cin(full_adder_12_cout), .S(out_3[13]), .Cout(full_adder_13_cout));
  full_adder full_adder_14 (.A(A[14]), .B(B14), .Cin(full_adder_13_cout), .S(out_3[14]), .Cout(full_adder_14_cout));
  full_adder full_adder_15 (.A(A[15]), .B(B15), .Cin(full_adder_14_cout), .S(out_3[15]), .Cout(full_adder_15_cout));
  full_adder full_adder_16 (.A(A[16]), .B(B16), .Cin(full_adder_15_cout), .S(out_3[16]), .Cout(full_adder_16_cout));
  full_adder full_adder_17 (.A(A[17]), .B(B17), .Cin(full_adder_16_cout), .S(out_3[17]), .Cout(full_adder_17_cout));
  full_adder full_adder_18 (.A(A[18]), .B(B18), .Cin(full_adder_17_cout), .S(out_3[18]), .Cout(full_adder_18_cout));
  full_adder full_adder_19 (.A(A[19]), .B(B19), .Cin(full_adder_18_cout), .S(out_3[19]), .Cout(full_adder_19_cout));
  full_adder full_adder_20 (.A(A[20]), .B(B20), .Cin(full_adder_19_cout), .S(out_3[20]), .Cout(full_adder_20_cout));
  full_adder full_adder_21 (.A(A[21]), .B(B21), .Cin(full_adder_20_cout), .S(out_3[21]), .Cout(full_adder_21_cout));
  full_adder full_adder_22 (.A(A[22]), .B(B22), .Cin(full_adder_21_cout), .S(out_3[22]), .Cout(full_adder_22_cout));
  full_adder full_adder_23 (.A(A[23]), .B(B23), .Cin(full_adder_22_cout), .S(out_3[23]), .Cout(full_adder_23_cout));
  full_adder full_adder_24 (.A(A[24]), .B(B24), .Cin(full_adder_23_cout), .S(out_3[24]), .Cout(full_adder_24_cout));
  full_adder full_adder_25 (.A(A[25]), .B(B25), .Cin(full_adder_24_cout), .S(out_3[25]), .Cout(full_adder_25_cout));
  full_adder full_adder_26 (.A(A[26]), .B(B26), .Cin(full_adder_25_cout), .S(out_3[26]), .Cout(full_adder_26_cout));
  full_adder full_adder_27 (.A(A[27]), .B(B27), .Cin(full_adder_26_cout), .S(out_3[27]), .Cout(full_adder_27_cout));
  full_adder full_adder_28 (.A(A[28]), .B(B28), .Cin(full_adder_27_cout), .S(out_3[28]), .Cout(full_adder_28_cout));
  full_adder full_adder_29 (.A(A[29]), .B(B29), .Cin(full_adder_28_cout), .S(out_3[29]), .Cout(full_adder_29_cout));
  full_adder full_adder_30 (.A(A[30]), .B(B30), .Cin(full_adder_29_cout), .S(out_3[30]), .Cout(full_adder_30_cout));
  full_adder full_adder_31 (.A(A[31]), .B(B31), .Cin(full_adder_30_cout), .S(out_3[31]));  // open: Cout

  // Other names for the same wires on the sheet: S0 = out_3[0]; S1 = out_3[1]; S2 = out_3[2]; S3 = out_3[3];
  //   S4 = out_3[4]; S5 = out_3[5]; S6 = out_3[6]; S7 = out_3[7]; S8 = out_3[8]; S9 = out_3[9]; S10 = out_3[10];
  //   S11 = out_3[11]; S12 = out_3[12]; S13 = out_3[13]; S14 = out_3[14]; S15 = out_3[15]; S16 = out_3[16];
  //   S17 = out_3[17]; S18 = out_3[18]; S19 = out_3[19]; S20 = out_3[20]; S21 = out_3[21]; S22 = out_3[22];
  //   S23 = out_3[23]; S24 = out_3[24]; S25 = out_3[25]; S26 = out_3[26]; S27 = out_3[27]; S28 = out_3[28];
  //   S29 = out_3[29]; S30 = out_3[30]; S31 = out_3[31]
endmodule

module teste (
  input  [31:0] A,
  output [23:0] S
);


  assign S = A[31:8];
endmodule

module AluControl (
  input  [2:0] Func3,
  input  [6:0] Func7,
  input  [1:0] AluOP,
  output Bit0,
  output Bit1,
  output Bit2,
  output Bit3
);

  wire and_1_out, and_2_out, and_3_out, and_4_out, and_5_out, and_6_out, and_7_out, and_8_out, and_9_out,
       and_10_out, not_1_out, not_2_out, not_3_out, not_4_out, not_5_out, not_6_out, not_7_out, not_8_out,
       not_9_out, not_10_out, not_11_out, not_12_out, not_13_out, not_14_out, not_15_out, or_2_out;

  not not_1 (not_1_out, Func3[0]);
  not not_2 (not_2_out, Func7[5]);
  not not_3 (not_3_out, AluOP[0]);
  not not_4 (not_4_out, Func3[2]);
  not not_5 (not_5_out, Func3[1]);
  not not_6 (not_6_out, not_1_out);
  not not_7 (not_7_out, AluOP[0]);
  and and_1 (and_1_out, not_4_out, not_5_out, not_6_out, not_2_out, AluOP[1], not_7_out);
  not not_8 (not_8_out, Func3[2]);
  not not_9 (not_9_out, Func3[2]);
  not not_10 (not_10_out, Func3[1]);
  not not_11 (not_11_out, Func3[2]);
  not not_12 (not_12_out, AluOP[1]);
  and and_2 (and_2_out, not_1_out, Func3[1], Func3[2], not_2_out, not_3_out, AluOP[1]);
  not not_13 (not_13_out, Func3[1]);
  and and_3 (and_3_out, not_8_out, not_1_out);
  not not_14 (not_14_out, AluOP[0]);
  and and_4 (and_4_out, not_9_out, not_10_out, not_11_out);
  not not_15 (not_15_out, AluOP[1]);
  and and_5 (and_5_out, Func7[5], AluOP[1], not_14_out, and_4_out);
  and and_6 (and_6_out, and_4_out, not_12_out, AluOP[0]);
  or or_1 (Bit0, and_1_out, and_2_out);
  and and_7 (and_7_out, not_13_out, not_3_out, AluOP[1], not_3_out, and_3_out);
  and and_8 (and_8_out, not_13_out, Func7[5], AluOP[1], not_3_out, and_3_out);
  and and_9 (and_9_out, Func3[1], not_15_out, not_3_out, and_3_out);
  and and_10 (and_10_out, not_13_out, not_15_out, AluOP[0], and_3_out);
  or or_2 (or_2_out, and_5_out, and_6_out);
  or or_3 (Bit1, and_7_out, and_8_out, and_9_out, and_10_out);
  or or_4 (Bit2, and_1_out, or_2_out);

  assign Bit3 = 1'b0;
endmodule

module Zeroverifyer (
  input  [31:0] in_1,
  output out_2
);

  wire nor_1_out, nor_2_out, nor_3_out, nor_4_out;

  nor nor_1 (nor_1_out, in_1[0], in_1[1], in_1[2], in_1[3], in_1[4], in_1[5], in_1[6], in_1[7]);
  nor nor_2 (nor_2_out, in_1[8], in_1[9], in_1[10], in_1[11], in_1[12], in_1[13], in_1[14], in_1[15]);
  nor nor_3 (nor_3_out, in_1[16], in_1[17], in_1[18], in_1[19], in_1[20], in_1[21], in_1[22], in_1[23]);
  nor nor_4 (nor_4_out, in_1[24], in_1[25], in_1[26], in_1[27], in_1[28], in_1[29], in_1[30], in_1[31]);
  and and_1 (out_2, nor_1_out, nor_2_out, nor_3_out, nor_4_out);
endmodule

module ImediateGenerator (
  input  [31:0] in_1,
  input  [6:0] Opcode,
  output [31:0] S
);

  wire [19:0] demultiplexer_1_out0;
  wire [24:0] demultiplexer_1_out1, demultiplexer_1_out3;
  wire [31:0] demultiplexer_1_out0_2, demultiplexer_1_out1_2;
  wire [31:1] demultiplexer_1_out3_2;

  Demultiplexer #(.select(2), .width(32)) demultiplexer_1 (
    .out0({demultiplexer_1_out0_2[31], demultiplexer_1_out0_2[10:0], demultiplexer_1_out0}),
    .out1({demultiplexer_1_out1_2[31], demultiplexer_1_out1_2[10:5], demultiplexer_1_out1[24:12], demultiplexer_1_out1_2[4:0], demultiplexer_1_out1[6:0]}),
    .out3({demultiplexer_1_out3_2[31], demultiplexer_1_out3_2[10:5], demultiplexer_1_out3[24:12], demultiplexer_1_out3_2[4:1], demultiplexer_1_out3_2[11], demultiplexer_1_out3[6:0]}),
    .in(in_1), .sel(Opcode[6:5]));  // open: out2
  Multiplexer #(.select(2), .width(32)) multiplexer_1 (
    .in0({{21{demultiplexer_1_out0_2[31]}}, demultiplexer_1_out0_2[10:0]}),
    .in1({{21{demultiplexer_1_out1_2[31]}}, demultiplexer_1_out1_2[10:0]}),
    .in3({{20{demultiplexer_1_out3_2[31]}}, demultiplexer_1_out3_2[11:1], 1'b0}), .out(S), .sel(Opcode[6:5]));  // open: in2
endmodule

module HazardDetectionUnit (
  input  IDEXMemRead,
  input  MEM_WRITE,
  input  [4:0] IFIDRegisterRs,
  input  [4:0] IDEXRegisterRD,
  input  [4:0] IFIDRegisterRt,
  output S
);

  wire and_1_out, Igual2_out, Igual_out, not_1_out, or_1_out, xnor_1_out, xnor_2_out, xnor_3_out, xnor_4_out,
       xnor_5_out, xnor_6_out, xnor_7_out, xnor_8_out, xnor_9_out, xnor_10_out;

  not not_1 (not_1_out, MEM_WRITE);
  xnor xnor_1 (xnor_1_out, IFIDRegisterRs[0], IDEXRegisterRD[0]);
  xnor xnor_2 (xnor_2_out, IFIDRegisterRs[1], IDEXRegisterRD[1]);
  xnor xnor_3 (xnor_3_out, IFIDRegisterRs[2], IDEXRegisterRD[2]);
  xnor xnor_4 (xnor_4_out, IFIDRegisterRs[3], IDEXRegisterRD[3]);
  xnor xnor_5 (xnor_5_out, IFIDRegisterRs[4], IDEXRegisterRD[4]);
  xnor xnor_6 (xnor_6_out, IDEXRegisterRD[0], IFIDRegisterRt[0]);
  xnor xnor_7 (xnor_7_out, IDEXRegisterRD[1], IFIDRegisterRt[1]);
  xnor xnor_8 (xnor_8_out, IDEXRegisterRD[2], IFIDRegisterRt[2]);
  xnor xnor_9 (xnor_9_out, IDEXRegisterRD[3], IFIDRegisterRt[3]);
  xnor xnor_10 (xnor_10_out, IDEXRegisterRD[4], IFIDRegisterRt[4]);
  and Igual (Igual_out, xnor_1_out, xnor_2_out, xnor_3_out, xnor_4_out, xnor_5_out);
  and Igual2 (Igual2_out, xnor_6_out, xnor_7_out, xnor_8_out, xnor_9_out, xnor_10_out);
  or or_1 (or_1_out, Igual_out, Igual2_out);
  and and_1 (and_1_out, IDEXMemRead, not_1_out, or_1_out);
  not not_2 (S, and_1_out);
endmodule

module forwarding_unit (
  input  MEM_RegWrite,
  input  EX_RegWrite,
  input  [4:0] EX_RegisterRD,
  input  [4:0] ID_RegisterRS,
  input  [4:0] MEM_RegisterRD,
  input  ALUSRC,
  input  [4:0] ID_RegisterRT,
  output [1:0] ForwardA,
  output [1:0] ForwardB
);

  wire and_1_out, and_2_out, Dif2_out, Dif_out, Igual2_out, Igual3_out, Igual4_out, Igual_out, not_1_out,
       not_2_out, not_3_out, or_1_out, or_2_out, xnor_1_out, xnor_2_out, xnor_3_out, xnor_4_out, xnor_5_out,
       xnor_6_out, xnor_7_out, xnor_8_out, xnor_9_out, xnor_10_out, xnor_11_out, xnor_12_out, xnor_13_out,
       xnor_14_out, xnor_15_out, xnor_16_out, xnor_17_out, xnor_18_out, xnor_19_out, xnor_20_out,
       xnor_21_out, xnor_22_out, xnor_23_out, xnor_24_out, xnor_25_out, xor_1_out, xor_2_out, xor_3_out,
       xor_4_out, xor_5_out;

  or or_1 (or_1_out, MEM_RegisterRD[0], MEM_RegisterRD[1], MEM_RegisterRD[2], MEM_RegisterRD[3], MEM_RegisterRD[4]);
  or or_2 (or_2_out, EX_RegisterRD[0], EX_RegisterRD[1], EX_RegisterRD[2], EX_RegisterRD[3], EX_RegisterRD[4]);
  xnor xnor_1 (xnor_1_out, EX_RegisterRD[0], ID_RegisterRS[0]);
  xnor xnor_2 (xnor_2_out, EX_RegisterRD[1], ID_RegisterRS[1]);
  xnor xnor_3 (xnor_3_out, EX_RegisterRD[2], ID_RegisterRS[2]);
  xnor xnor_4 (xnor_4_out, EX_RegisterRD[3], ID_RegisterRS[3]);
  xnor xnor_5 (xnor_5_out, EX_RegisterRD[4], ID_RegisterRS[4]);
  xnor xnor_6 (xnor_6_out, ID_RegisterRS[0], MEM_RegisterRD[0]);
  xnor xnor_7 (xnor_7_out, ID_RegisterRS[1], MEM_RegisterRD[1]);
  xnor xnor_8 (xnor_8_out, ID_RegisterRS[2], MEM_RegisterRD[2]);
  xnor xnor_9 (xnor_9_out, ID_RegisterRS[3], MEM_RegisterRD[3]);
  xnor xnor_10 (xnor_10_out, ID_RegisterRS[4], MEM_RegisterRD[4]);
  xnor xnor_11 (xnor_11_out, EX_RegisterRD[0], ID_RegisterRS[0]);
  xnor xnor_12 (xnor_12_out, EX_RegisterRD[1], ID_RegisterRS[1]);
  xnor xnor_13 (xnor_13_out, EX_RegisterRD[2], ID_RegisterRS[2]);
  xnor xnor_14 (xnor_14_out, EX_RegisterRD[3], ID_RegisterRS[3]);
  xnor xnor_15 (xnor_15_out, EX_RegisterRD[4], ID_RegisterRS[4]);
  xor xor_1 (xor_1_out, ID_RegisterRT[0], EX_RegisterRD[0]);
  xor xor_2 (xor_2_out, ID_RegisterRT[1], EX_RegisterRD[1]);
  xor xor_3 (xor_3_out, ID_RegisterRT[2], EX_RegisterRD[2]);
  xor xor_4 (xor_4_out, ID_RegisterRT[3], EX_RegisterRD[3]);
  xor xor_5 (xor_5_out, ID_RegisterRT[4], EX_RegisterRD[4]);
  xnor xnor_16 (xnor_16_out, ID_RegisterRT[0], MEM_RegisterRD[0]);
  xnor xnor_17 (xnor_17_out, ID_RegisterRT[1], MEM_RegisterRD[1]);
  xnor xnor_18 (xnor_18_out, ID_RegisterRT[2], MEM_RegisterRD[2]);
  xnor xnor_19 (xnor_19_out, ID_RegisterRT[3], MEM_RegisterRD[3]);
  xnor xnor_20 (xnor_20_out, ID_RegisterRT[4], MEM_RegisterRD[4]);
  xnor xnor_21 (xnor_21_out, ID_RegisterRT[0], EX_RegisterRD[0]);
  xnor xnor_22 (xnor_22_out, ID_RegisterRT[1], EX_RegisterRD[1]);
  xnor xnor_23 (xnor_23_out, ID_RegisterRT[2], EX_RegisterRD[2]);
  xnor xnor_24 (xnor_24_out, ID_RegisterRT[3], EX_RegisterRD[3]);
  xnor xnor_25 (xnor_25_out, ID_RegisterRT[4], EX_RegisterRD[4]);
  and Dif (Dif_out, xnor_1_out, xnor_2_out, xnor_3_out, xnor_4_out, xnor_5_out);
  and Igual (Igual_out, xnor_6_out, xnor_7_out, xnor_8_out, xnor_9_out, xnor_10_out);
  and Igual2 (Igual2_out, xnor_11_out, xnor_12_out, xnor_13_out, xnor_14_out, xnor_15_out);
  and Dif2 (Dif2_out, xor_1_out, xor_2_out, xor_3_out, xor_4_out, xor_5_out);
  and Igual3 (Igual3_out, xnor_16_out, xnor_17_out, xnor_18_out, xnor_19_out, xnor_20_out);
  and Igual4 (Igual4_out, xnor_21_out, xnor_22_out, xnor_23_out, xnor_24_out, xnor_25_out);
  and and_1 (and_1_out, EX_RegWrite, or_2_out, Dif_out);
  and and_2 (and_2_out, EX_RegWrite, or_2_out, Dif2_out);
  not not_1 (not_1_out, and_1_out);
  not not_2 (not_2_out, and_2_out);
  not not_3 (not_3_out, ALUSRC);
  and Bit0 (ForwardA[0], or_1_out, MEM_RegWrite, not_1_out, Igual_out);
  and Bit1 (ForwardA[1], EX_RegWrite, or_2_out, Igual2_out);
  and and_3 (ForwardB[0], not_2_out, not_3_out, Igual3_out, MEM_RegWrite, or_1_out);
  and and_4 (ForwardB[1], EX_RegWrite, or_2_out, not_3_out, Igual4_out);
endmodule

module Forwarding_MEM (
  input  REGWRITE_MEM,
  input  MEMWRITE_EX,
  input  [4:0] RD_MEM,
  input  [4:0] R2_EX,
  output Forwading
);

  wire Dif0_out, Igual_out, xnor_1_out, xnor_2_out, xnor_3_out, xnor_4_out, xnor_5_out;

  or Dif0 (Dif0_out, RD_MEM[0], RD_MEM[1], RD_MEM[2], RD_MEM[3], RD_MEM[4]);
  xnor xnor_1 (xnor_1_out, RD_MEM[0], R2_EX[0]);
  xnor xnor_2 (xnor_2_out, RD_MEM[1], R2_EX[1]);
  xnor xnor_3 (xnor_3_out, RD_MEM[2], R2_EX[2]);
  xnor xnor_4 (xnor_4_out, RD_MEM[3], R2_EX[3]);
  xnor xnor_5 (xnor_5_out, RD_MEM[4], R2_EX[4]);
  and Igual (Igual_out, xnor_1_out, xnor_2_out, xnor_3_out, xnor_4_out, xnor_5_out);
  and and_1 (Forwading, REGWRITE_MEM, MEMWRITE_EX, Dif0_out, Igual_out);
endmodule

module Forwarding_beq (
  input  RegWrite_ID,
  input  [4:0] RD_ID,
  input  MEM_RegWrite,
  input  EX_RegWrite,
  input  [4:0] EX_RegisterRD,
  input  [4:0] RS1,
  input  [4:0] MEM_RegisterRD,
  input  [4:0] RS2,
  output [1:0] ForwardA,
  output [1:0] ForwardB
);

  wire and_1_out, and_2_out, and_3_out, and_4_out, and_5_out, and_6_out, and_7_out, and_8_out, and_9_out,
       and_10_out, and_11_out, and_12_out, Dif2_out, Dif_out, Igual2_out, Igual3_out, Igual4_out, Igual_out,
       not_1_out, not_2_out, not_3_out, not_4_out, or_1_out, or_2_out, or_3_out, xnor_1_out, xnor_2_out,
       xnor_3_out, xnor_4_out, xnor_5_out, xnor_6_out, xnor_7_out, xnor_8_out, xnor_9_out, xnor_10_out,
       xnor_11_out, xnor_12_out, xnor_13_out, xnor_14_out, xnor_15_out, xnor_16_out, xnor_17_out,
       xnor_18_out, xnor_19_out, xnor_20_out, xnor_21_out, xnor_22_out, xnor_23_out, xnor_24_out,
       xnor_25_out, xnor_26_out, xnor_27_out, xnor_28_out, xnor_29_out, xnor_30_out, xnor_31_out,
       xnor_32_out, xnor_33_out, xnor_34_out, xnor_35_out, xor_1_out, xor_2_out, xor_3_out, xor_4_out,
       xor_5_out;

  or or_1 (or_1_out, MEM_RegisterRD[0], MEM_RegisterRD[1], MEM_RegisterRD[2], MEM_RegisterRD[3], MEM_RegisterRD[4]);
  or or_2 (or_2_out, RD_ID[0], RD_ID[1], RD_ID[2], RD_ID[3], RD_ID[4]);
  or or_3 (or_3_out, EX_RegisterRD[0], EX_RegisterRD[1], EX_RegisterRD[2], EX_RegisterRD[3], EX_RegisterRD[4]);
  xnor xnor_1 (xnor_1_out, RS2[0], RD_ID[0]);
  xnor xnor_2 (xnor_2_out, RS2[1], RD_ID[1]);
  xnor xnor_3 (xnor_3_out, RS2[2], RD_ID[2]);
  xnor xnor_4 (xnor_4_out, RS2[3], RD_ID[3]);
  xnor xnor_5 (xnor_5_out, RS2[4], RD_ID[4]);
  xnor xnor_6 (xnor_6_out, RD_ID[0], RS1[0]);
  xnor xnor_7 (xnor_7_out, RD_ID[1], RS1[1]);
  xnor xnor_8 (xnor_8_out, RD_ID[2], RS1[2]);
  xnor xnor_9 (xnor_9_out, RD_ID[3], RS1[3]);
  xnor xnor_10 (xnor_10_out, RD_ID[4], RS1[4]);
  xnor xnor_11 (xnor_11_out, EX_RegisterRD[0], RS1[0]);
  xnor xnor_12 (xnor_12_out, EX_RegisterRD[1], RS1[1]);
  xnor xnor_13 (xnor_13_out, EX_RegisterRD[2], RS1[2]);
  xnor xnor_14 (xnor_14_out, EX_RegisterRD[3], RS1[3]);
  xnor xnor_15 (xnor_15_out, EX_RegisterRD[4], RS1[4]);
  and and_1 (and_1_out, xnor_1_out, xnor_2_out, xnor_3_out, xnor_4_out, xnor_5_out);
  and and_2 (and_2_out, xnor_6_out, xnor_7_out, xnor_8_out, xnor_9_out, xnor_10_out);
  xnor xnor_16 (xnor_16_out, RS1[0], MEM_RegisterRD[0]);
  xnor xnor_17 (xnor_17_out, RS1[1], MEM_RegisterRD[1]);
  xnor xnor_18 (xnor_18_out, RS1[2], MEM_RegisterRD[2]);
  xnor xnor_19 (xnor_19_out, RS1[3], MEM_RegisterRD[3]);
  xnor xnor_20 (xnor_20_out, RS1[4], MEM_RegisterRD[4]);
  xnor xnor_21 (xnor_21_out, EX_RegisterRD[0], RS1[0]);
  xnor xnor_22 (xnor_22_out, EX_RegisterRD[1], RS1[1]);
  xnor xnor_23 (xnor_23_out, EX_RegisterRD[2], RS1[2]);
  xnor xnor_24 (xnor_24_out, EX_RegisterRD[3], RS1[3]);
  xnor xnor_25 (xnor_25_out, EX_RegisterRD[4], RS1[4]);
  xor xor_1 (xor_1_out, RS2[0], EX_RegisterRD[0]);
  xor xor_2 (xor_2_out, RS2[1], EX_RegisterRD[1]);
  xor xor_3 (xor_3_out, RS2[2], EX_RegisterRD[2]);
  xor xor_4 (xor_4_out, RS2[3], EX_RegisterRD[3]);
  xor xor_5 (xor_5_out, RS2[4], EX_RegisterRD[4]);
  xnor xnor_26 (xnor_26_out, RS2[0], MEM_RegisterRD[0]);
  xnor xnor_27 (xnor_27_out, RS2[1], MEM_RegisterRD[1]);
  xnor xnor_28 (xnor_28_out, RS2[2], MEM_RegisterRD[2]);
  xnor xnor_29 (xnor_29_out, RS2[3], MEM_RegisterRD[3]);
  xnor xnor_30 (xnor_30_out, RS2[4], MEM_RegisterRD[4]);
  xnor xnor_31 (xnor_31_out, RS2[0], EX_RegisterRD[0]);
  xnor xnor_32 (xnor_32_out, RS2[1], EX_RegisterRD[1]);
  xnor xnor_33 (xnor_33_out, RS2[2], EX_RegisterRD[2]);
  xnor xnor_34 (xnor_34_out, RS2[3], EX_RegisterRD[3]);
  xnor xnor_35 (xnor_35_out, RS2[4], EX_RegisterRD[4]);
  and Dif (Dif_out, xnor_11_out, xnor_12_out, xnor_13_out, xnor_14_out, xnor_15_out);
  and Igual (Igual_out, xnor_16_out, xnor_17_out, xnor_18_out, xnor_19_out, xnor_20_out);
  and Igual2 (Igual2_out, xnor_21_out, xnor_22_out, xnor_23_out, xnor_24_out, xnor_25_out);
  and Dif2 (Dif2_out, xor_1_out, xor_2_out, xor_3_out, xor_4_out, xor_5_out);
  and Igual3 (Igual3_out, xnor_26_out, xnor_27_out, xnor_28_out, xnor_29_out, xnor_30_out);
  and Igual4 (Igual4_out, xnor_31_out, xnor_32_out, xnor_33_out, xnor_34_out, xnor_35_out);
  and and_3 (and_3_out, EX_RegWrite, or_3_out, Dif_out);
  and and_4 (and_4_out, EX_RegWrite, or_3_out, Dif2_out);
  not not_1 (not_1_out, and_3_out);
  not not_2 (not_2_out, and_4_out);
  and and_5 (and_5_out, or_2_out, and_2_out, RegWrite_ID);
  and and_6 (and_6_out, or_1_out, MEM_RegWrite, not_3_out, not_1_out, Igual_out);
  and and_7 (and_7_out, EX_RegWrite, or_3_out, not_3_out, Igual2_out);
  and and_8 (and_8_out, and_1_out, RegWrite_ID, or_2_out);
  and and_9 (and_9_out, not_2_out, Igual3_out, not_4_out, MEM_RegWrite, or_1_out);
  and and_10 (and_10_out, or_2_out, and_2_out, RegWrite_ID);
  not not_3 (not_3_out, and_10_out);
  or bit0 (ForwardA[0], and_5_out, and_6_out);
  or bit1 (ForwardA[1], and_5_out, and_7_out);
  and and_11 (and_11_out, EX_RegWrite, or_3_out, not_4_out, Igual4_out);
  or or_4 (ForwardB[0], and_8_out, and_9_out);
  or or_5 (ForwardB[1], and_8_out, and_11_out);
  and and_12 (and_12_out, and_1_out, RegWrite_ID, or_2_out);
  not not_4 (not_4_out, and_12_out);
endmodule

module IF_ID (
  input  DEU_BRANCH,
  input  [31:0] D_PC,
  input  W,
  input  R,
  input  CLK,
  input  [31:0] D_INS,
  output DEU_BRANCH_ID,
  output [31:0] S_PC_IF,
  output [31:0] S_INS_IF
);

  D_Flip_Flop d_ff_1 (.D(DEU_BRANCH), .clk(CLK), .Q(DEU_BRANCH_ID), .reset(R));  // open: Qn, preset
  Registrador_32bits PC (.W0(W), .CLK(CLK), .R(R), .D(D_PC), .S(S_PC_IF));
  Registrador_32bits INS (.W0(W), .CLK(CLK), .R(R), .D(D_INS), .S(S_INS_IF));
endmodule

module ID_EX (
  input  [31:0] PC,
  input  CLK,
  input  W,
  input  R,
  input  [31:0] Ra,
  input  [31:0] Rb,
  input  [31:0] IMM,
  input  [4:0] RD,
  input  [2:0] FUNCT3,
  input  [4:0] RS1_5BITS,
  input  [4:0] RS2_5BITS,
  input  [6:0] Funct7,
  output [31:0] S_PC_ID,
  output [31:0] S_Ra_ID,
  output [31:0] S_Rb_ID,
  output [31:0] S_IMM_ID,
  output [4:0] S_RD_ID,
  output [2:0] FUNCT3_ID,
  output [4:0] S_RS1_ID,
  output [4:0] S_RS2_ID,
  output [6:0] S_Funct7
);

  D_Flip_Flop d_ff_1 (.D(FUNCT3[0]), .clk(CLK), .Q(FUNCT3_ID[0]), .reset(R));  // open: Qn, preset
  D_Flip_Flop d_ff_2 (.D(FUNCT3[1]), .clk(CLK), .Q(FUNCT3_ID[1]), .reset(R));  // open: Qn, preset
  D_Flip_Flop d_ff_3 (.D(FUNCT3[2]), .clk(CLK), .Q(FUNCT3_ID[2]), .reset(R));  // open: Qn, preset
  Registrador_32bits registrador_32bits_1 (.W0(W), .CLK(CLK), .R(R), .D(PC), .S(S_PC_ID));
  Registrador_32bits registrador_32bits_2 (.W0(W), .CLK(CLK), .R(R), .D(Ra), .S(S_Ra_ID));
  Registrador_32bits registrador_32bits_3 (.W0(W), .CLK(CLK), .R(R), .D(Rb), .S(S_Rb_ID));
  Registrador_32bits registrador_32bits_4 (.W0(W), .CLK(CLK), .R(R), .D(IMM), .S(S_IMM_ID));
  D_Flip_Flop d_ff_4 (.D(RD[0]), .clk(CLK), .Q(S_RD_ID[0]), .reset(R));  // open: Qn, preset
  D_Flip_Flop d_ff_5 (.D(RD[1]), .clk(CLK), .Q(S_RD_ID[1]), .reset(R));  // open: Qn, preset
  D_Flip_Flop d_ff_6 (.D(RD[2]), .clk(CLK), .Q(S_RD_ID[2]), .reset(R));  // open: Qn, preset
  D_Flip_Flop d_ff_7 (.D(RD[3]), .clk(CLK), .Q(S_RD_ID[3]), .reset(R));  // open: Qn, preset
  D_Flip_Flop d_ff_8 (.D(RD[4]), .clk(CLK), .Q(S_RD_ID[4]), .reset(R));  // open: Qn, preset
  D_Flip_Flop d_ff_9 (.D(RS1_5BITS[0]), .clk(CLK), .Q(S_RS1_ID[0]), .reset(R));  // open: Qn, preset
  D_Flip_Flop d_ff_10 (.D(RS1_5BITS[1]), .clk(CLK), .Q(S_RS1_ID[1]), .reset(R));  // open: Qn, preset
  D_Flip_Flop d_ff_11 (.D(RS1_5BITS[2]), .clk(CLK), .Q(S_RS1_ID[2]), .reset(R));  // open: Qn, preset
  D_Flip_Flop d_ff_12 (.D(RS1_5BITS[3]), .clk(CLK), .Q(S_RS1_ID[3]), .reset(R));  // open: Qn, preset
  D_Flip_Flop d_ff_13 (.D(RS1_5BITS[4]), .clk(CLK), .Q(S_RS1_ID[4]), .reset(R));  // open: Qn, preset
  D_Flip_Flop d_ff_14 (.D(RS2_5BITS[0]), .clk(CLK), .Q(S_RS2_ID[0]), .reset(R));  // open: Qn, preset
  D_Flip_Flop d_ff_15 (.D(RS2_5BITS[1]), .clk(CLK), .Q(S_RS2_ID[1]), .reset(R));  // open: Qn, preset
  D_Flip_Flop d_ff_16 (.D(RS2_5BITS[2]), .clk(CLK), .Q(S_RS2_ID[2]), .reset(R));  // open: Qn, preset
  D_Flip_Flop d_ff_17 (.D(RS2_5BITS[3]), .clk(CLK), .Q(S_RS2_ID[3]), .reset(R));  // open: Qn, preset
  D_Flip_Flop d_ff_18 (.D(RS2_5BITS[4]), .clk(CLK), .Q(S_RS2_ID[4]), .reset(R));  // open: Qn, preset
  D_Flip_Flop d_ff_19 (.D(Funct7[0]), .clk(CLK), .Q(S_Funct7[0]), .reset(R));  // open: Qn, preset
  D_Flip_Flop d_ff_20 (.D(Funct7[1]), .clk(CLK), .Q(S_Funct7[1]), .reset(R));  // open: Qn, preset
  D_Flip_Flop d_ff_21 (.D(Funct7[2]), .clk(CLK), .Q(S_Funct7[2]), .reset(R));  // open: Qn, preset
  D_Flip_Flop d_ff_22 (.D(Funct7[3]), .clk(CLK), .Q(S_Funct7[3]), .reset(R));  // open: Qn, preset
  D_Flip_Flop d_ff_23 (.D(Funct7[4]), .clk(CLK), .Q(S_Funct7[4]), .reset(R));  // open: Qn, preset
  D_Flip_Flop d_ff_24 (.D(Funct7[5]), .clk(CLK), .Q(S_Funct7[5]), .reset(R));  // open: Qn, preset
  D_Flip_Flop d_ff_25 (.D(Funct7[6]), .clk(CLK), .Q(S_Funct7[6]), .reset(R));  // open: Qn, preset
endmodule

module EX_MEM (
  input  [31:0] SOMADOR,
  input  CLK,
  input  R,
  input  W,
  input  ZERO_VER,
  input  [31:0] ULA,
  input  [31:0] R2,
  input  [4:0] RD_ID,
  input  [4:0] RS2_ID,
  output [31:0] S_SOMADOR_EX,
  output S_ZERO_VER_EX,
  output [31:0] S_ULA_EX,
  output [31:0] S_R2_EX,
  output [4:0] RD_EX,
  output [4:0] S_RS2_EX
);

  wire undriven;

  D_Flip_Flop d_ff_1 (.D(RS2_ID[0]), .clk(CLK), .Q(S_RS2_EX[0]), .reset(R));  // open: Qn, preset
  D_Flip_Flop d_ff_2 (.D(RS2_ID[1]), .clk(CLK), .Q(S_RS2_EX[1]), .reset(R));  // open: Qn, preset
  D_Flip_Flop d_ff_3 (.D(RS2_ID[2]), .clk(CLK), .Q(S_RS2_EX[2]), .reset(R));  // open: Qn, preset
  D_Flip_Flop d_ff_4 (.D(RS2_ID[3]), .clk(CLK), .Q(S_RS2_EX[3]), .reset(R));  // open: Qn, preset
  D_Flip_Flop d_ff_5 (.D(RS2_ID[4]), .clk(CLK), .Q(S_RS2_EX[4]), .reset(R));  // open: Qn, preset
  D_Flip_Flop d_ff_6 (.D(RD_ID[0]), .clk(CLK), .Q(RD_EX[0]), .reset(R));  // open: Qn, preset
  D_Flip_Flop d_ff_7 (.D(RD_ID[1]), .clk(CLK), .Q(RD_EX[1]), .reset(R));  // open: Qn, preset
  D_Flip_Flop d_ff_8 (.D(RD_ID[2]), .clk(CLK), .Q(RD_EX[2]), .reset(R));  // open: Qn, preset
  D_Flip_Flop d_ff_9 (.D(RD_ID[3]), .clk(CLK), .Q(RD_EX[3]), .reset(R));  // open: Qn, preset
  D_Flip_Flop d_ff_10 (.D(RD_ID[4]), .clk(CLK), .Q(RD_EX[4]), .reset(R));  // open: Qn, preset
  D_Flip_Flop d_ff_11 (.D(ZERO_VER), .clk(CLK), .Q(S_ZERO_VER_EX), .preset(undriven), .reset(R));  // open: Qn
  Registrador_32bits registrador_32bits_1 (.W0(W), .CLK(CLK), .R(R), .D(ULA), .S(S_ULA_EX));
  Registrador_32bits registrador_32bits_2 (.W0(W), .CLK(CLK), .R(R), .D(R2), .S(S_R2_EX));
  Registrador_32bits registrador_32bits_3 (.W0(W), .CLK(CLK), .R(R), .D(SOMADOR), .S(S_SOMADOR_EX));
endmodule

module MEM_WB (
  input  W,
  input  R,
  input  CLK,
  input  [31:0] READ_DATA,
  input  [31:0] ALU,
  input  [4:0] RD_EX,
  output [31:0] S_READ_DATA_MEM,
  output [31:0] S_ALU_MEM,
  output [4:0] RD_MEM
);

  D_Flip_Flop d_ff_1 (.D(RD_EX[0]), .clk(CLK), .Q(RD_MEM[0]), .reset(R));  // open: Qn, preset
  D_Flip_Flop d_ff_2 (.D(RD_EX[1]), .clk(CLK), .Q(RD_MEM[1]), .reset(R));  // open: Qn, preset
  D_Flip_Flop d_ff_3 (.D(RD_EX[2]), .clk(CLK), .Q(RD_MEM[2]), .reset(R));  // open: Qn, preset
  D_Flip_Flop d_ff_4 (.D(RD_EX[3]), .clk(CLK), .Q(RD_MEM[3]), .reset(R));  // open: Qn, preset
  D_Flip_Flop d_ff_5 (.D(RD_EX[4]), .clk(CLK), .Q(RD_MEM[4]), .reset(R));  // open: Qn, preset
  Registrador_32bits registrador_32bits_1 (.W0(W), .CLK(CLK), .R(R), .D(READ_DATA), .S(S_READ_DATA_MEM));
  Registrador_32bits registrador_32bits_2 (.W0(W), .CLK(CLK), .R(R), .D(ALU), .S(S_ALU_MEM));
endmodule

module UC_ID_EX (
  input  MEMREAD,
  input  MEMTOREG,
  input  MEMWRITE,
  input  UC_ALUSRC,
  input  CLK,
  input  R,
  input  UC_BRANCH,
  input  [1:0] UC_ALUOP,
  input  REGWRITE,
  output S_MEMREAD_ID,
  output S_MEMTOREG_ID,
  output S_MEMWRITE_ID,
  output S_ALUSRC_ID,
  output S_BRANCH_ID,
  output [1:0] S_ALUOP_ID,
  output S_REGWRITE_ID
);

  D_Flip_Flop d_ff_1 (.D(MEMREAD), .clk(CLK), .Q(S_MEMREAD_ID), .reset(R));  // open: Qn, preset
  D_Flip_Flop d_ff_2 (.D(MEMTOREG), .clk(CLK), .Q(S_MEMTOREG_ID), .reset(R));  // open: Qn, preset
  D_Flip_Flop d_ff_3 (.D(MEMWRITE), .clk(CLK), .Q(S_MEMWRITE_ID), .reset(R));  // open: Qn, preset
  D_Flip_Flop d_ff_4 (.D(UC_ALUSRC), .clk(CLK), .Q(S_ALUSRC_ID), .reset(R));  // open: Qn, preset
  D_Flip_Flop d_ff_5 (.D(UC_BRANCH), .clk(CLK), .Q(S_BRANCH_ID), .reset(R));  // open: Qn, preset
  D_Flip_Flop d_ff_6 (.D(UC_ALUOP[0]), .clk(CLK), .Q(S_ALUOP_ID[0]), .reset(R));  // open: Qn, preset
  D_Flip_Flop d_ff_7 (.D(UC_ALUOP[1]), .clk(CLK), .Q(S_ALUOP_ID[1]), .reset(R));  // open: Qn, preset
  D_Flip_Flop d_ff_8 (.D(REGWRITE), .clk(CLK), .Q(S_REGWRITE_ID), .reset(R));  // open: Qn, preset
endmodule

module UC_EX_MEM (
  input  BRANCH,
  input  MEMREAD_EX,
  input  MEMTOREG_EX,
  input  R,
  input  CLK,
  input  MEMWRITE_EX,
  input  REGWRITE_ID,
  output BRANCH_EX,
  output S_MEMREAD_EX,
  output S_MEMTOREG_EX,
  output S_MEMWRITE_EX,
  output S_REGWRITE_EX
);

  D_Flip_Flop d_ff_1 (.D(BRANCH), .clk(CLK), .Q(BRANCH_EX), .reset(R));  // open: Qn, preset
  D_Flip_Flop d_ff_2 (.D(MEMREAD_EX), .clk(CLK), .Q(S_MEMREAD_EX), .reset(R));  // open: Qn, preset
  D_Flip_Flop d_ff_3 (.D(MEMTOREG_EX), .clk(CLK), .Q(S_MEMTOREG_EX), .reset(R));  // open: Qn, preset
  D_Flip_Flop d_ff_4 (.D(MEMWRITE_EX), .clk(CLK), .Q(S_MEMWRITE_EX), .reset(R));  // open: Qn, preset
  D_Flip_Flop d_ff_5 (.D(REGWRITE_ID), .clk(CLK), .Q(S_REGWRITE_EX), .reset(R));  // open: Qn, preset
endmodule

module UC_MEM_WB (
  input  WB_EX,
  input  CLK,
  input  R,
  input  REGWRITE_EX,
  output WB_MEM,
  output S_REGWRITE_MEM
);

  D_Flip_Flop d_ff_1 (.D(REGWRITE_EX), .clk(CLK), .Q(S_REGWRITE_MEM), .reset(R));  // open: Qn, preset
  D_Flip_Flop d_ff_2 (.D(WB_EX), .clk(CLK), .Q(WB_MEM), .reset(R));  // open: Qn, preset
endmodule
